# Fritzing sketch AssignmentSchematics (saved by Fritzing 0.9.3b)
breadboards: 1

parts:
  Part1 = Arduino Uno (Rev3) - ICSP
  U1 = POT [package=pot_alpha_rv16af-20]
  U2 = POT [package=pot_alpha_rv16af-20]
  U3 = POT [package=pot_alpha_rv16af-20]

nets:
  N1: Part1.A0, U1.S
  N2: Part1.A1, U2.S
  N3: Part1.A2, U3.S
  N4: Part1.5V, U1.E, U2.E, U3.E
  N5: Part1.GND, U1.A, U2.A, U3.A
